# Fritzing sketch laser_tx (saved by Fritzing 1.0.5)

parts:
  Mod1 = KY-008 Laser Transmitter Module [package="Breakout board"]
  S1 = Square Pushbutton
  VCC1 = 4 x AAA Battery Mount [internal_resistance=0.1Ω]  # not connected

nets:
  N1: Mod1.S, S1.leg1

custom parts:
  KY-008 Laser Transmitter Module: KY-008 Laser Transmitter Module, emits a dot shaped red laser beam.
